# Fritzing sketch circuit-diagram (saved by Fritzing 0.9.3b)
breadboards: 1

parts:
  Raspberry_Pi_1 = Raspberry Pi 3 [part_number=RPI-3-V1.2]
  DHT1 = DHT22 Humidity and Temperature Sensor
  DS1 = DS18B20 1-Wire Temperature Sensor [part_number=DS18B20]
  R1 = Resistor [tolerance=±5% resistance=4.7k package=THT]
  R2 = Resistor [tolerance=±5% resistance=4.7k package=THT]

nets:
  VDD: Raspberry_Pi_1.3v3, DHT1.VDD, DS1.VDD, R1.Pin_1, R2.Pin_0
  N1: Raspberry_Pi_1.GPIO4, DS1.DQ, R1.Pin_0
  N2: Raspberry_Pi_1.GPIO14, DHT1.DATA, R2.Pin_1
  GND: Raspberry_Pi_1.GND, DHT1.GND, DS1.GND
